// Logisim project Simple_8_CPU.circ as structural Verilog: 5 circuits, main circuit main
module main (
);

  wire alu_control_1_out_8, Carry_flag, clock_1_out, Imm_Select, Jump_select, MemToReg, Read, Write,
       Zero_flag;
  wire [2:0] alu_control_1_out_4;
  wire [7:0] ALU_OUTPUT, Immediate8, multiplexer_1_out, program_counter_1_pc, RAM_OUTPUT,
       register_specification_1_output_a, register_specification_1_output_b, WriteData;
  wire [15:0] FARF_data;

  Program_Counter program_counter_1 (.Jump_Select(Jump_select), .Jump_Address(Immediate8), .PC(program_counter_1_pc));
  ROM #(.dataWidth(16)) FARF (.addr(program_counter_1_pc), .data(FARF_data));
  Multiplexer #(.width(8)) multiplexer_1 (
    .in0(ALU_OUTPUT), .in1(Immediate8), .out(multiplexer_1_out), .sel(Imm_Select));
  assign Immediate8 = {{3{1'b0}}, FARF_data[4:0]};  // Bit_Extender bit_extender_1
  Multiplexer #(.width(8)) multiplexer_2 (.in0(multiplexer_1_out), .in1(RAM_OUTPUT), .out(WriteData), .sel(MemToReg));
  ALU_CONTROL alu_control_1 (
    .Opcode_In(FARF_data[15:11]), .Carry_flag(Carry_flag), .Zero_flag(Zero_flag), .MemToReg(MemToReg),
    .Imm_Select(Imm_Select), .Jump_Select(Jump_select), .out_5(Write), .out_7(Read),
    .out_8(alu_control_1_out_8), .out_4(alu_control_1_out_4));
  Register_Specification register_specification_1 (
    .Read_Address_B(FARF_data[10:8]), .Read_Address_A(FARF_data[7:5]), .WriteData(WriteData),
    .WE(alu_control_1_out_8), .WriteAddr(FARF_data[10:8]), .OUTPUT_A(register_specification_1_output_a),
    .OUTPUT_B(register_specification_1_output_b));
  Clock clock_1 (.out(clock_1_out));
  RAM ram_1 (
    .addr(Immediate8), .we(Write), .oe(Read), .clk(clock_1_out), .din(register_specification_1_output_b),
    .dout(RAM_OUTPUT));
  ALU alu_1 (
    .ALU_S(alu_control_1_out_4), .A(register_specification_1_output_a),
    .B(register_specification_1_output_b), .Carry_flag(Carry_flag), .out_5(ALU_OUTPUT), .Zero_flag(Zero_flag));

  // Notes on the sheet:
  //   contents of FARF (hex, n*v repeats v):
  //   4805 4903 20
endmodule

module Register_Specification (
  input  [2:0] Read_Address_A,
  input  [7:0] WriteData,
  input  WE,
  input  [2:0] WriteAddr,
  input  [2:0] Read_Address_B,
  output [7:0] OUTPUT_A,
  output [7:0] OUTPUT_B
);

  wire button_1_out, clock_1_out, demultiplexer_1_out0, demultiplexer_1_out1, demultiplexer_1_out2,
       demultiplexer_1_out3, demultiplexer_1_out4, demultiplexer_1_out5, demultiplexer_1_out6,
       demultiplexer_1_out7;
  wire [7:0] R0_q, R1_q, R2_q, R3_q, R4_q, R5_q, R6_q, R7_q;

  Demultiplexer #(.select(3)) demultiplexer_1 (
    .out0(demultiplexer_1_out0), .out1(demultiplexer_1_out1), .out2(demultiplexer_1_out2),
    .out3(demultiplexer_1_out3), .out4(demultiplexer_1_out4), .out5(demultiplexer_1_out5),
    .out6(demultiplexer_1_out6), .out7(demultiplexer_1_out7), .in(WE), .sel(WriteAddr));
  Clock clock_1 (.out(clock_1_out));
  Button button_1 (.out(button_1_out));
  Register R0 (.D(WriteData), .en(demultiplexer_1_out0), .clk(clock_1_out), .Q(R0_q), .clr(button_1_out));
  Register R1 (.D(WriteData), .en(demultiplexer_1_out1), .clk(clock_1_out), .Q(R1_q), .clr(button_1_out));
  Register R2 (.D(WriteData), .en(demultiplexer_1_out2), .clk(clock_1_out), .Q(R2_q), .clr(button_1_out));
  Register R3 (.D(WriteData), .en(demultiplexer_1_out3), .clk(clock_1_out), .Q(R3_q), .clr(button_1_out));
  Register R4 (.D(WriteData), .en(demultiplexer_1_out4), .clk(clock_1_out), .Q(R4_q), .clr(button_1_out));
  Register R5 (.D(WriteData), .en(demultiplexer_1_out5), .clk(clock_1_out), .Q(R5_q), .clr(button_1_out));
  Register R6 (.D(WriteData), .en(demultiplexer_1_out6), .clk(clock_1_out), .Q(R6_q), .clr(button_1_out));
  Register R7 (.D(WriteData), .en(demultiplexer_1_out7), .clk(clock_1_out), .Q(R7_q), .clr(button_1_out));
  Multiplexer #(.select(3), .width(8)) multiplexer_1 (
    .in0(R0_q), .in1(R1_q), .in2(R2_q), .in3(R3_q), .in4(R4_q), .in5(R5_q), .in6(R6_q), .in7(R7_q),
    .out(OUTPUT_A), .sel(Read_Address_A));
  Multiplexer #(.select(3), .width(8)) multiplexer_2 (
    .in0(R0_q), .in1(R1_q), .in2(R2_q), .in3(R3_q), .in4(R4_q), .in5(R5_q), .in6(R6_q), .in7(R7_q),
    .out(OUTPUT_B), .sel(Read_Address_B));
endmodule

module Program_Counter (
  input  Jump_Select,
  input  [7:0] Jump_Address,
  output [7:0] PC
);

  wire button_1_out, clock_1_out;
  wire [7:0] adder_1_out, multiplexer_1_out;

  Adder adder_1 (.a(8'h1), .b(PC), .out(adder_1_out));  // open: cin, cout
  Multiplexer #(.width(8)) multiplexer_1 (
    .in0(adder_1_out), .in1(Jump_Address), .out(multiplexer_1_out), .sel(Jump_Select));
  Clock clock_1 (.out(clock_1_out));
  Register register_1 (.D(multiplexer_1_out), .en(1'b1), .clk(clock_1_out), .Q(PC), .clr(button_1_out));
  Button button_1 (.out(button_1_out));
endmodule

module ALU (
  input  [7:0] A,
  input  [7:0] B,
  input  [2:0] ALU_S,
  output Carry_flag,
  output [7:0] out_5,
  output Zero_flag
);

  wire [7:0] adder_1_out, and_1_out, nor_1_out, not_1_out, or_1_out, subtractor_1_out;

  Adder adder_1 (.a(A), .b(B), .out(adder_1_out), .cout(Carry_flag));  // open: cin
  Subtractor subtractor_1 (.a(A), .b(B), .out(subtractor_1_out));  // open: bin, bout
  assign and_1_out = A & B;  // AND_Gate and_1, 8 bits wide
  assign or_1_out = A | B;  // OR_Gate or_1, 8 bits wide
  assign nor_1_out = ~(A | B);  // NOR_Gate nor_1, 8 bits wide
  assign not_1_out = ~A;  // NOT_Gate not_1, 8 bits wide
  Multiplexer #(.select(3), .width(8)) multiplexer_1 (
    .in0(adder_1_out), .in1(subtractor_1_out), .in2(and_1_out), .in3(or_1_out), .in4(nor_1_out),
    .in5(not_1_out), .in6({8{1'b0}}), .in7({8{1'b0}}), .out(out_5), .sel(ALU_S));
  nor nor_2 (Zero_flag, out_5[0], out_5[1], out_5[2], out_5[3], out_5[4], out_5[5], out_5[6], out_5[7]);

  // Other names for the same wires on the sheet: ALU_OUTPUT[7:0] = out_5
endmodule

module ALU_CONTROL (
  input  [4:0] Opcode_In,
  input  Zero_flag,
  input  Carry_flag,
  output [2:0] out_4,
  output out_5,
  output MemToReg,
  output out_7,
  output out_8,
  output Imm_Select,
  output Jump_Select
);

  wire decoder_1_out15, decoder_1_out16, decoder_1_out17, decoder_1_out18, decoder_1_out19, decoder_1_out20,
       decoder_1_out21, decoder_1_out22, decoder_1_out23, decoder_1_out24, decoder_1_out25, decoder_1_out26,
       decoder_1_out27, decoder_1_out28, decoder_1_out29, decoder_1_out30, decoder_1_out31, INST_ADD,
       INST_AND, INST_HLT, INST_JC, INST_JMP, INST_JNZ, INST_JZ, INST_MOV, INST_NOT, INST_OR, INST_SUB,
       INST_XOR, JC, JNZ, JZ, not_1_out;

  Decoder #(.enable("false"), .select(5)) decoder_1 (
    .out0(INST_ADD), .out1(INST_SUB), .out2(INST_AND), .out3(INST_OR), .out4(INST_XOR), .out5(INST_NOT),
    .out6(MemToReg), .out7(out_5), .out8(INST_MOV), .out9(Imm_Select), .out10(INST_JMP), .out11(INST_JZ),
    .out12(INST_JNZ), .out13(INST_JC), .out14(INST_HLT), .out15(decoder_1_out15), .out16(decoder_1_out16),
    .out17(decoder_1_out17), .out18(decoder_1_out18), .out19(decoder_1_out19), .out20(decoder_1_out20),
    .out21(decoder_1_out21), .out22(decoder_1_out22), .out23(decoder_1_out23), .out24(decoder_1_out24),
    .out25(decoder_1_out25), .out26(decoder_1_out26), .out27(decoder_1_out27), .out28(decoder_1_out28),
    .out29(decoder_1_out29), .out30(decoder_1_out30), .out31(decoder_1_out31), .sel(Opcode_In));
  or or_1 (Jump_Select, INST_JMP, JZ, JNZ, JC);
  not not_1 (not_1_out, Zero_flag);
  and and_1 (JZ, INST_JZ, Zero_flag);
  and and_2 (JNZ, INST_JNZ, not_1_out);
  and and_3 (JC, INST_JC, Carry_flag);
  or or_2 (out_4[0], INST_SUB, INST_OR, INST_NOT);
  or or_3 (out_4[1], INST_AND, INST_OR);
  or or_4 (out_4[2], INST_XOR, INST_NOT);
  or or_5 (out_8, INST_ADD, INST_SUB, INST_OR, INST_XOR, INST_NOT, MemToReg, INST_MOV, Imm_Select, INST_AND);

  assign out_7 = MemToReg;
  // also tied to GND on the sheet: {decoder_1_out15, decoder_1_out16, decoder_1_out17, decoder_1_out18, decoder_1_out19, decoder_1_out20, decoder_1_out21, decoder_1_out22, decoder_1_out23, decoder_1_out24, decoder_1_out25, decoder_1_out26, decoder_1_out27, decoder_1_out28, decoder_1_out29, decoder_1_out30, decoder_1_out31}

  // Other names for the same wires on the sheet: ALU_Control[2:0] = out_4; INST_LDI = Imm_Select; JMP = INST_JMP;
  //   INST_LOAD = MemToReg; MemRead = MemToReg; INST_STORE = out_5; MemWrite = out_5; RegWrite = out_8
endmodule
